// Digital circuit byte_add.dig as structural Verilog
module byte_add (
  input  [7:0] I0,
  input  [7:0] I1,
  output CF,
  output OF,
  output [7:0] O
);

  wire _1bit_add_1_carry_out, _1bit_add_2_carry_out, _1bit_add_3_carry_out, _1bit_add_4_carry_out,
       _1bit_add_5_carry_out, _1bit_add_6_carry_out, _1bit_add_7_carry_out;

  _1bit_add _1bit_add_1 (.I0(I0[0]), .I1(I1[0]), .CARRY_IN(1'b0), .O(O[0]), .CARRY_OUT(_1bit_add_1_carry_out));
  _1bit_add _1bit_add_2 (
    .I0(I0[1]), .I1(I1[1]), .CARRY_IN(_1bit_add_1_carry_out), .O(O[1]), .CARRY_OUT(_1bit_add_2_carry_out));
  _1bit_add _1bit_add_3 (
    .I0(I0[2]), .I1(I1[2]), .CARRY_IN(_1bit_add_2_carry_out), .O(O[2]), .CARRY_OUT(_1bit_add_3_carry_out));
  _1bit_add _1bit_add_4 (
    .I0(I0[3]), .I1(I1[3]), .CARRY_IN(_1bit_add_3_carry_out), .O(O[3]), .CARRY_OUT(_1bit_add_4_carry_out));
  _1bit_add _1bit_add_5 (
    .I0(I0[4]), .I1(I1[4]), .CARRY_IN(_1bit_add_4_carry_out), .O(O[4]), .CARRY_OUT(_1bit_add_5_carry_out));
  _1bit_add _1bit_add_6 (
    .I0(I0[5]), .I1(I1[5]), .CARRY_IN(_1bit_add_5_carry_out), .O(O[5]), .CARRY_OUT(_1bit_add_6_carry_out));
  _1bit_add _1bit_add_7 (
    .I0(I0[6]), .I1(I1[6]), .CARRY_IN(_1bit_add_6_carry_out), .O(O[6]), .CARRY_OUT(_1bit_add_7_carry_out));
  _1bit_add _1bit_add_8 (.I0(I0[7]), .I1(I1[7]), .CARRY_IN(_1bit_add_7_carry_out), .O(O[7]), .CARRY_OUT(CF));
  xor xor_1 (OF, CF, _1bit_add_7_carry_out);
endmodule
